# Fritzing sketch Device (saved by Fritzing 0.9.3b)

parts:
  WeMos_D1_Mini1 = WeMos D1 Mini
  D1 = LTE-302 [package=lte-302]

nets:
  N1: WeMos_D1_Mini1.D6, D1.A
  N2: WeMos_D1_Mini1.D8, D1.C

notes:
  Ground => D6
  Signal => D8
